# Fritzing sketch mega (saved by Fritzing 0.9.0b)
breadboards: 1

parts:
  Part1 = Arduino Mega 2560 (Rev3)
  NRF24L2 = NRF24L01
  C3 = Capacitor Polarized [package=cpol-radial-10uf-25v]
  Part2 = Adafruit MAX9814 Electret Microphone Amplifier [part_number="Adafruit #1713"]

nets:
  N1: Part1.A0, Part2.OUTPUT
  3V3: Part1.3V3, NRF24L2.VCC, C3.+, Part2.VDD, Part2.GAIN
  GND: Part1.GND, NRF24L2.GND, C3.-, Part2.GND
  N2: Part1.D40, NRF24L2.CE
  N3: Part1.D50, NRF24L2.MISO
  N4: Part1.D51, NRF24L2.MOSI
  N5: Part1.D52, NRF24L2.SCK
  N6: Part1.D53, NRF24L2.CSN

custom parts:
  NRF24L01: NRF24L01 module
  Adafruit MAX9814 Electret Microphone Amplifier: Add an ear to your project with this well-designed electret microphone amplifier with AGC. This fully assembled and tested board comes with a 20-20KHz electret microphone soldered on. For the amplification, we use the Maxim MAX9814, a specialty chip that is designed for amplifying electret microphones in situations where the loudness of the audio isn't predictable. This fancy microphone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
